# Fritzing sketch wiring_gateway (saved by Fritzing 0.9.3b)
circuit board: 8.46667cm x 5.64444cm

parts:
  Bauteil1 = Arduino Pro Mini (3.3V)
  Bauteil2 = NRF24L01+ Breakout Board

nets:
  VCC: Bauteil1.VCC, Bauteil2.VCC
  GND: Bauteil1.GND, Bauteil2.GND
  N1: Bauteil1.SCK, Bauteil2.SCK
  N2: Bauteil1.MISO, Bauteil2.MISO
  N3: Bauteil1.MOSI, Bauteil2.MOSI
  N4: Bauteil1.D10, Bauteil2.CS
  N5: Bauteil1.D9, Bauteil2.CE
